# Fritzing sketch Motor Wiring (saved by Fritzing 0.9.8b)

parts:
  Mod1 = Raspberry Pi 4B
  M1 = gear-motor
  S1 = H-Bridge with L298N
  M2 = gear-motor
  M3 = gear-motor
  M4 = gear-motor
  S2 = H-Bridge with L298N
  BATT1 = 4xAA Switchable Battery Pack w/JST connector

nets:
  N1: Mod1.GPIO14, S1.IN1
  N2: Mod1.GPIO15, S1.IN2
  N3: Mod1.GPIO18, S1.IN3
  N4: Mod1.GPIO23, S1.IN4
  N5: Mod1.GPIO24, S2.IN1
  N6: Mod1.GPIO25, S2.IN2
  N7: Mod1.GPIO8, S2.IN3
  N8: Mod1.GPIO7, S2.IN4
  N9: M1.pin_1, S1.M2-01
  N10: M1.pin_2, S1.M2-02
  N11: S1.12V, BATT1.POS
  N12: S1.GND, BATT1.NEG
  N13: S1.M1-01, M2.pin_2
  N14: S1.M1-02, M2.pin_1
  N15: M3.pin_1, S2.M1-02
  N16: M3.pin_2, S2.M1-01
  N17: M4.pin_1, S2.M2-02
  N18: M4.pin_2, S2.M2-01

notes:
  The Pi is to be powered via USB for this test.
  Do not connect the +, red terminal of the battery to the Pi.
  Motor power supply
  GND of Pi connected to this circuit

custom parts:
  H-Bridge with L298N: h-bridge
  4xAA Switchable Battery Pack w/JST connector: 4xAA Switchable Battery Pack with JST connector
